# Fritzing sketch Controller (saved by Fritzing 0.7.5b)
breadboards: 2

parts:
  RST = Pushbutton [package="[THT]"]
  XTAL1 = Crystal [frequency="16 Mhz" package=THT]
  LCD1 = LCD screen
  LED1 = LED - 5mm [color="White (6500K)" package="5 mm [THT]"]
  R4 = Resistor [tolerance=±5% resistance=220 package=THT]
  RFID1 = RFID Reader
  R6 = Resistor [tolerance=±5% resistance=1k package=THT]
  C5 = Ceramic Capacitor [capacitance=22pF package="100 mil [THT, multilayer]"]
  C6 = Ceramic Capacitor [capacitance=22pF package="100 mil [THT, multilayer]"]
  C11 = Ceramic Capacitor [capacitance=100nF package="100 mil [THT, multilayer]"]
  LED2 = LED - 5mm [color="White (6500K)" package="5 mm [THT]"]
  - = Screw terminal - 2 pins [package=THT]
  + = Screw terminal - 2 pins [package=THT]
  Reset = Screw terminal - 2 pins [package=THT]
  U1 = atmega328 [package=dip]
  Speaker = Screw terminal - 2 pins [package=THT]
  FTDI = male pin header, 6 pins [form="♂ (male)"]
  FTDI1 = shrouded pin header, 6 pins [form="♂ (shrouded male)"]
  R8 = Resistor [tolerance=±5% resistance=10k package=THT]
  R7 = Resistor [tolerance=±5% resistance=10k package=THT]
  R5 = Resistor [tolerance=±5% resistance=10k package=THT]
  R2 = Resistor [tolerance=±5% resistance=10k package=THT]
  Contrast = male pin header, 3 pins [form="♂ (male)"]
  C12 = Electrolytic Capacitor [capacitance=10µF package="100 mil [THT, electrolytic]"]

nets:
  N1: RST.Pin_1, RST.Pin_2, C11.0, U1.RESET, R2.Pin_1
  GND: RST.Pin_3, RST.Pin_4, LCD1.VSS, LCD1.R/W, LCD1.LED-, R4.Pin_0, RFID1.GND, RFID1.+/-, R6.Pin_1, C5.1, C6.0, -.pin2, +.pin2, Reset.pin2, U1.GND, Speaker.pin1, FTDI.pin6, FTDI1.pin5, Contrast.pin1, C12.-
  N2: XTAL1.pin_0, C6.1, U1.XLAT1
  N3: XTAL1.pin_1, C5.0, U1.XLAT2
  VDD: LCD1.VDD, LCD1.LED+, RFID1.RES, RFID1.+5V, LED2.anode, U1.VCC, U1.AVCC, U1.AREF, FTDI.pin4, FTDI.pin5, FTDI1.pin4, R8.Pin_0, R7.Pin_0, R5.Pin_0, R2.Pin_0, Contrast.pin3, C12.+
  N4: LCD1.V0, Contrast.pin2
  N5: LCD1.RS, U1.D12
  N6: LCD1.E, U1.D11_(PWM)
  N7: LCD1.DB4, U1.D5_(PWM)
  N8: LCD1.DB5, U1.D4
  N9: LCD1.DB6, U1.D3_(PWM)
  N10: LCD1.DB7, U1.D2
  N11: LED1.cathode, R4.Pin_1
  N12: LED1.anode, U1.D7
  N13: RFID1.D0, U1.D8
  N14: R6.Pin_0, LED2.cathode
  N15: C11.1, FTDI.pin1
  N16: -.pin1, U1.A3, R8.Pin_1
  N17: +.pin1, U1.A2, R7.Pin_1
  N18: Reset.pin1, U1.D9_(PWM), R5.Pin_1
  N19: U1.D0_(RX), FTDI.pin3
  N20: U1.D1_(TX), FTDI.pin2
  N21: U1.D10_(PWM), Speaker.pin2
  N22: U1.A4, FTDI1.pin1
  N23: U1.A5, FTDI1.pin6

notes:
  1.0
  www.sidlee.com
