# Fritzing sketch Motherboard (saved by Fritzing 0.7.7b)
breadboards: 3

parts:
  7805 = Voltage Regulator - 5V [package="TO220 [THT]"]
  7-16V_DC = Power plug
  RST = Pushbutton [package="[THT]"]
  C2 = Electrolytic Capacitor [capacitance=10µF rated_voltage=35V package="100 mil [THT, electrolytic]"]
  C1 = Electrolytic Capacitor [capacitance=10µF rated_voltage=35V package="100 mil [THT, electrolytic]"]
  XTAL1 = Crystal [frequency="16 Mhz" package=THT]
  U3 = 74HC595 [package="DIP16 [THT]"]
  U4 = 74HC595 [package="DIP16 [THT]"]
  U5 = 74HC595 [package="DIP16 [THT]"]
  C7 = Ceramic Capacitor [capacitance=100nF package="100 mil [THT, multilayer]"]
  R17 = Resistor [tolerance=±5% resistance=10k package=THT]
  R18 = Resistor [tolerance=±5% resistance=10k package=THT]
  PWR = LED - 5mm [color="White (8000K)" package="5 mm [THT]"]
  R19 = Resistor [tolerance=±5% resistance=1k package=THT]
  LZRin1 = Screw terminal - 2 pins [package=THT]
  C5 = Ceramic Capacitor [capacitance=22pF package="100 mil [THT, multilayer]"]
  C6 = Ceramic Capacitor [capacitance=22pF package="100 mil [THT, multilayer]"]
  FTDI = male pin header, 6 pins [form="♂ (male)"]
  C11 = Ceramic Capacitor [capacitance=100nF package="100 mil [THT, multilayer]"]
  R20 = Resistor [tolerance=±5% resistance=330 package=THT]
  R22 = Resistor [tolerance=±5% resistance=220 package=THT]
  R23 = Resistor [tolerance=±5% resistance=220 package=THT]
  R24 = Resistor [tolerance=±5% resistance=220 package=THT]
  R25 = Resistor [tolerance=±5% resistance=220 package=THT]
  R26 = Resistor [tolerance=±5% resistance=220 package=THT]
  R27 = Resistor [tolerance=±5% resistance=220 package=THT]
  R28 = Resistor [tolerance=±5% resistance=220 package=THT]
  R29 = Resistor [tolerance=±5% resistance=220 package=THT]
  R30 = Resistor [tolerance=±5% resistance=220 package=THT]
  R31 = Resistor [tolerance=±5% resistance=220 package=THT]
  R32 = Resistor [tolerance=±5% resistance=220 package=THT]
  R33 = Resistor [tolerance=±5% resistance=220 package=THT]
  R34 = Resistor [tolerance=±5% resistance=220 package=THT]
  R35 = Resistor [tolerance=±5% resistance=220 package=THT]
  R36 = Resistor [tolerance=±5% resistance=220 package=THT]
  R37 = Resistor [tolerance=±5% resistance=220 package=THT]
  R38 = Resistor [tolerance=±5% resistance=220 package=THT]
  R39 = Resistor [tolerance=±5% resistance=220 package=THT]
  R40 = Resistor [tolerance=±5% resistance=220 package=THT]
  R43 = Resistor [tolerance=±5% resistance=220 package=THT]
  SCR_GND = Screw terminal - 2 pins [package=THT]
  R44 = Resistor [tolerance=±5% resistance=330 package=THT]
  GOAL1 = Screw terminal - 2 pins [package=THT]
  GOAL2 = Screw terminal - 2 pins [package=THT]
  J2 = shrouded pin header, 10 pins [form="♂ (shrouded male)"]
  J1 = shrouded pin header, 10 pins [form="♂ (shrouded male)"]
  OUT1 = shrouded pin header, 6 pins [form="♂ (shrouded male)"]
  OUT2 = shrouded pin header, 6 pins [form="♂ (shrouded male)"]
  U2 = atmega328 [package=dip]
  LZR1 = screw terminal, 3 pins
  LZR2 = screw terminal, 3 pins
  J3 = female pin header, 11 pins [form="♀ (female)"]  # not connected
  J4 = female pin header, 11 pins [form="♀ (female)"]
  LD33V = Voltage Regulator - 3.3V [package="TO220 [THT]"]
  3_3V_|_5V = Logic Level Converter
  C15 = Electrolytic Capacitor [capacitance=10µF rated_voltage=35V package="100 mil [THT, electrolytic]"]
  R2 = Resistor [tolerance=±5% resistance=10k package=THT]
  LZRin2 = Screw terminal - 2 pins [package=THT]

nets:
  N1: 7805.input_voltage, 7-16V_DC.VCC, C1.+
  GND: 7805.GND, 7-16V_DC.GND, RST.Pin_3, RST.Pin_4, C2.-, C1.-, U3.GND, U3.OE, U4.GND, U4.OE, U5.GND, U5.OE, C7.0, R17.Pin_0, R18.Pin_0, PWR.cathode, C5.1, C6.0, FTDI.pin5, FTDI.pin6, R20.Pin_0, SCR_GND.pin1, SCR_GND.pin2, R44.Pin_0, OUT1.pin2, OUT2.pin2, U2.GND, LZR1.pin2, LZR2.pin2, J4.pin1, LD33V.input_voltage, 3_3V_|_5V.GND, C15.-
  VCC: 7805.output_voltage, C2.+, U3.MR, U3.VCC, U4.MR, U4.VCC, U5.MR, U5.VCC, R19.Pin_0, LZRin1.pin2, FTDI.pin4, OUT1.pin1, OUT2.pin1, U2.VCC, U2.AVCC, U2.AREF, LZR1.pin1, LZR2.pin1, LD33V.output_voltage, 3_3V_|_5V.HV, R2.Pin_0, LZRin2.pin2
  N2: RST.Pin_1, RST.Pin_2, C11.1, U2.RESET, R2.Pin_1
  N3: XTAL1.pin_0, C6.1, U2.XLAT1
  N4: XTAL1.pin_1, C5.0, U2.XLAT2
  N5: U3.Q1, R27.Pin_1
  N6: U3.Q2, R26.Pin_1
  N7: U3.Q3, R25.Pin_1
  N8: U3.Q4, R24.Pin_1
  N9: U3.Q5, R23.Pin_1
  N10: U3.Q6, R22.Pin_1
  N11: U3.Q7, R31.Pin_1
  N12: U3.Q7', U4.DS
  N13: U3.SH_CP, U4.SH_CP, U5.SH_CP, U2.D2
  N14: U3.ST_CP, U4.ST_CP, U5.ST_CP, C7.1, U2.D8
  N15: U3.DS, U2.D3_(PWM)
  N16: U3.Q0, R28.Pin_1
  N17: U4.Q1, R29.Pin_1
  N18: U4.Q2, R38.Pin_1
  N19: U4.Q3, R34.Pin_1
  N20: U4.Q4, R33.Pin_1
  N21: U4.Q5, R37.Pin_1
  N22: U4.Q6, R36.Pin_1
  N23: U4.Q7, R35.Pin_1
  N24: U4.Q7', U5.DS
  N25: U4.Q0, R30.Pin_1
  N26: U5.Q1, R43.Pin_1
  N27: U5.Q2, R40.Pin_1
  N28: U5.Q3, R39.Pin_1
  N29: U5.Q0, R32.Pin_1
  N30: R17.Pin_1, U2.A2, LZRin2.pin1
  N31: R18.Pin_1, LZRin1.pin1, U2.A3
  N32: PWR.anode, R19.Pin_1
  N33: FTDI.pin1, C11.0
  N34: FTDI.pin2, U2.D1_(TX)
  N35: FTDI.pin3, U2.D0_(RX)
  N36: R20.Pin_1, GOAL1.pin2
  N37: R22.Pin_0, J1.pin6
  N38: R23.Pin_0, J1.pin7
  N39: R24.Pin_0, J1.pin8
  N40: R25.Pin_0, J1.pin9
  N41: R26.Pin_0, J1.pin10
  N42: R27.Pin_0, J1.pin1
  N43: R28.Pin_0, J1.pin2
  N44: R29.Pin_0, J1.pin3
  N45: R30.Pin_0, J1.pin4
  N46: R31.Pin_0, J1.pin5
  N47: R32.Pin_0, J2.pin7
  N48: R33.Pin_0, J2.pin1
  N49: R34.Pin_0, J2.pin2
  N50: R35.Pin_0, J2.pin8
  N51: R36.Pin_0, J2.pin9
  N52: R37.Pin_0, J2.pin10
  N53: R38.Pin_0, J2.pin3
  N54: R39.Pin_0, J2.pin4
  N55: R40.Pin_0, J2.pin5
  N56: R43.Pin_0, J2.pin6
  N57: R44.Pin_1, GOAL2.pin2
  N58: GOAL1.pin1, U2.D9_(PWM)
  N59: GOAL2.pin1, U2.D10_(PWM)
  N60: OUT1.pin3, OUT2.pin3, U2.A5
  N61: OUT1.pin4, OUT2.pin4, U2.A4
  N62: U2.D4, 3_3V_|_5V.TX2_HV
  N63: U2.D11_(PWM), LZR1.pin3, LZR2.pin3
  N64: U2.D13, 3_3V_|_5V.TX_HV
  N65: J4.pin2, LD33V.GND, 3_3V_|_5V.LV, C15.+
  N66: J4.pin3, 3_3V_|_5V.TX2_LV
  N67: J4.pin4, 3_3V_|_5V.TX_LV

notes:
  1.0
  www.sidlee.com
